# Fritzing sketch schematic (saved by Fritzing 0.9.3b)

parts:
  Raspberry_Pi_1 = Raspberry Pi 3 [part_number=RPI-3-V1.2]
  WeMos_D1_Mini_Relay_Shield_V1 = WeMos D1 Mini Relay Shield V2
  WeMos_D1_Mini_Relay_Shield_V2 = WeMos D1 Mini Relay Shield V2
  Part1 = Adafruit DC+Stepper Motor HAT [part_number="Adafruit #2348"]
  V1 = DC Power [voltage=5]
  M3 = Stepper Motor - Bipolar
  M4 = Stepper Motor - Bipolar
  J1 = Basic Servo

nets:
  3V3: Raspberry_Pi_1.3v3, Raspberry_Pi_1.3V3, Part1.3.3V
  N1: Raspberry_Pi_1.GPIO2, Part1.SDA
  N2: Raspberry_Pi_1.GPIO3, Part1.SCL
  N3: Raspberry_Pi_1.GPIO4, Part1.GPIO4
  GND: Raspberry_Pi_1.GND, Raspberry_Pi_1.GPIO20, Raspberry_Pi_1.GPIO8, WeMos_D1_Mini_Relay_Shield_V1.G, WeMos_D1_Mini_Relay_Shield_V2.G, Part1.GND, V1.V-, J1.gnd
  N4: Raspberry_Pi_1.GPIO17, Part1.GPIO17
  N5: Raspberry_Pi_1.GPIO27, Part1.GPIO27
  N6: Raspberry_Pi_1.GPIO22, Part1.GPIO22
  N7: Raspberry_Pi_1.GPIO10, Part1.SPI_MOSI
  N8: Raspberry_Pi_1.GPIO24, WeMos_D1_Mini_Relay_Shield_V2.A0, Part1.GPIO24
  N9: Raspberry_Pi_1.GPIO23, WeMos_D1_Mini_Relay_Shield_V1.A0, Part1.GPIO23
  N10: Raspberry_Pi_1.GPIO18, Part1.GPIO18, J1.pulse
  N11: Raspberry_Pi_1.GPIO15, Part1.RXD
  N12: Raspberry_Pi_1.GPIO14, Part1.TXD
  5V: Raspberry_Pi_1.5V, WeMos_D1_Mini_Relay_Shield_V1.5V, WeMos_D1_Mini_Relay_Shield_V2.5V, Part1.5.0V, J1.vcc
  N13: Part1.M2A, M3.D
  N14: Part1.M2B, M3.B
  N15: Part1.M1B, M3.C
  N16: Part1.M1A, M3.A
  N17: Part1.M4A, M4.D
  N18: Part1.M4B, M4.B
  N19: Part1.M3B, M4.C
  N20: Part1.M3A, M4.A
  N21: Part1.VMOTOR, V1.V+

custom parts:
  Adafruit DC+Stepper Motor HAT: Let your robotic dreams come true with the new DC+Stepper Motor HAT from Adafruit. This Raspberry Pi add-on is perfect for any motion project as it can drive up to 4 DC or 2 Stepper motors with full PWM speed control. Since the Raspberry Pi does not have a lot of PWM pins, we use a fully-dedicated PWM driver chip onboard to both control motor direction and speed. This chip handles all the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
